// Logisim project MNSK2.circ as structural Verilog: 1 circuit, main circuit main
module main (
  input  in_1,
  input  in_2,
  input  in_3,
  input  in_4,
  input  in_5,
  input  in_6,
  input  in_7,
  input  in_8,
  input  in_9,
  input  in_10,
  input  in_11,
  input  in_12,
  input  in_13,
  input  in_14,
  input  in_15,
  input  in_16,
  input  in_17,
  input  in_18,
  input  in_19,
  input  in_20,
  input  in_21,
  input  in_22,
  input  in_23,
  input  in_24,
  input  in_25,
  input  in_26,
  input  in_27,
  input  in_28,
  input  in_29,
  input  in_30,
  input  in_31,
  input  in_32,
  input  in_33,
  input  in_34,
  input  in_35,
  input  in_36,
  input  in_37,
  input  in_38,
  input  in_39,
  input  in_40,
  input  in_41,
  input  in_42
);

  wire and_1_out, and_2_out, and_3_out, or_1_out, or_2_out, or_3_out, or_4_out, or_5_out, or_6_out, or_7_out,
       or_8_out, or_9_out, or_10_out, or_11_out, or_12_out, or_13_out, or_14_out, or_15_out, or_16_out,
       or_17_out, or_18_out, or_19_out, or_20_out, or_21_out, or_22_out, or_23_out, or_24_out, or_25_out,
       or_26_out, or_27_out, or_28_out, or_29_out, or_30_out, undriven, undriven_2, undriven_3, undriven_4,
       undriven_5, undriven_6, undriven_7, undriven_8, undriven_9, undriven_10, undriven_11, undriven_12,
       undriven_13, undriven_14, undriven_15, undriven_16, undriven_17, undriven_18, undriven_19, undriven_20;

  or or_1 (or_1_out, in_1, in_2, undriven);
  or or_2 (or_2_out, undriven, in_3, in_4, undriven_2);
  or or_3 (or_3_out, undriven_2, in_5, in_6, undriven_3);
  or or_4 (or_4_out, undriven_3, in_7, in_8, undriven_4);
  or or_5 (or_5_out, undriven_4, in_9, in_10, undriven_5);
  or or_6 (or_6_out, undriven_5, in_11, in_12, undriven_6);
  or or_7 (or_7_out, undriven_6, in_13, in_14, undriven_7);
  or or_8 (or_8_out, undriven_7, in_15, in_16, undriven_8);
  or or_9 (or_9_out, undriven_8, in_17, in_18, undriven_9);
  or or_10 (or_10_out, undriven_9, in_19, in_20, undriven_10);
  or or_11 (or_11_out, undriven_10, in_21, in_22, undriven_11);
  or or_12 (or_12_out, undriven_11, in_23, in_24, undriven_12);
  or or_13 (or_13_out, undriven_12, in_25, in_26, undriven_13);
  or or_14 (or_14_out, undriven_13, in_27, in_28, undriven_14);
  or or_15 (or_15_out, undriven_14, in_29, in_30, undriven_15);
  or or_16 (or_16_out, undriven_15, in_31, in_32, undriven_16);
  or or_17 (or_17_out, undriven_16, in_33, in_34, undriven_17);
  or or_18 (or_18_out, undriven_17, in_35, in_36, undriven_18);
  or or_19 (or_19_out, undriven_18, in_37, in_38, undriven_19);
  or or_20 (or_20_out, undriven_19, in_39, in_40, undriven_20);
  or or_21 (or_21_out, undriven_20, in_41, in_42);
  or or_22 (or_22_out, or_1_out, or_2_out, or_3_out);
  or or_23 (or_23_out, or_4_out, or_5_out, or_6_out);
  or or_24 (or_24_out, or_7_out, or_8_out, or_9_out);
  or or_25 (or_25_out, or_10_out, or_11_out, or_12_out);
  or or_26 (or_26_out, or_13_out, or_14_out, or_15_out);
  or or_27 (or_27_out, or_16_out, or_17_out, or_18_out);
  or or_28 (or_28_out, or_19_out, or_20_out, or_21_out);
  or or_29 (or_29_out, or_22_out, or_23_out);
  or or_30 (or_30_out, or_27_out, or_28_out);
  and and_1 (and_1_out, or_24_out, or_26_out);
  and and_2 (and_2_out, or_29_out, or_30_out);
  and and_3 (and_3_out, or_25_out, and_2_out);
  LED led_1 (.in(and_1_out));
  LED led_2 (.in(and_3_out));

  // Notes on the sheet:
  //   если частица - горит один
  //   если волна - оба
endmodule
